# Fritzing sketch PSER (saved by Fritzing 0.9.3b)
breadboards: 1

parts:
  LED1 = LED - 3mm [color="Red (635nm)" package="3 mm [THT]"]
  LED2 = LED - 3mm [color="Blue (430nm)" package="3 mm [THT]"]
  LED3 = LED - 3mm [color="Green (555nm)" package="3 mm [THT]"]
  R3 = Resistor [tolerance=±5% resistance=330 package="0805 [SMD]"]
  R4 = Resistor [tolerance=±5% resistance=330 package="0805 [SMD]"]
  LCD1 = LCD screen
  LCM1602_IIC1 = LCM1602 IIC [part_number="LCM1602 IIC" chip_label="LCM1602 IIC" package="DIP (Dual Inline) [THT]"]
  Componente1 = Arduino Board Ethernet
  J1 = Piezo Speaker
  R5 = Resistor [tolerance=±5% resistance=220 package="0805 [SMD]"]
  Componente2 = RFID-RC522-v2
  R2 = Resistor [tolerance=±5% resistance=330 package="2512 [SMD]"]

nets:
  N1: LED1.cathode, R2.Pin_0
  N2: LED1.anode, Componente1.D7
  N3: LED2.cathode, R3.Pin_0
  N4: LED2.anode, Componente1.D6_PWM
  N5: LED3.cathode, R4.Pin_0
  N6: LED3.anode, Componente1.D5_PWM
  GND: R3.Pin_1, R4.Pin_1, LCM1602_IIC1.GND, Componente1.GND, R5.Pin_1, Componente2.GND, R2.Pin_1
  VSS: LCD1.VSS, LCM1602_IIC1.VSS
  VDD: LCD1.VDD, LCM1602_IIC1.VDD
  N7: LCD1.V0, LCM1602_IIC1.V0
  N8: LCD1.RS, LCM1602_IIC1.RS
  N9: LCD1.R/W, LCM1602_IIC1.RW
  N10: LCD1.E, LCM1602_IIC1.E
  N11: LCD1.DB0, LCM1602_IIC1.D0
  N12: LCD1.DB1, LCM1602_IIC1.D1
  N13: LCD1.DB2, LCM1602_IIC1.D2
  N14: LCD1.DB3, LCM1602_IIC1.D3
  N15: LCD1.DB4, LCM1602_IIC1.D4
  N16: LCD1.DB5, LCM1602_IIC1.D5
  N17: LCD1.DB6, LCM1602_IIC1.D6
  N18: LCD1.DB7, LCM1602_IIC1.D7
  N19: LCD1.LED+, LCM1602_IIC1.A
  N20: LCD1.LED-, LCM1602_IIC1.K
  N21: LCM1602_IIC1.LED_A, LCM1602_IIC1.LED_B
  N22: Componente1.D8, Componente2.SDA
  N23: Componente1.D9_PWM, Componente2.RST
  N24: Componente1.D11/MOSI, Componente2.MOSI
  N25: Componente1.D12/MISO, Componente2.MISO
  N26: Componente1.D13/SCK, Componente2.SCK
  N27: Componente1.D2_PWM, J1.pin2
  3V3: Componente1.3V3, Componente2.3.3V
  N28: J1.pin1, R5.Pin_0

custom parts:
  LCM1602 IIC: I2C-Module to use a 1602 or 2004 LCD on with the wire.h libory Serial LCD Modul
  RFID-RC522-v2: A simple China made RFID-RC522 Reader; do check the pin labels, as this is a MFRC522 based clone.
